// Logisim project 32 Bit Register.circ as structural Verilog: 2 circuits, main circuit main
module main (
  input  [4:0] Write_Register,
  input  [4:0] Read_Register_1,
  input  [4:0] Read_Register_2,
  input  [31:0] Write_Data,
  input  Reg_Write,
  output [31:0] Read_Data_1,
  output [31:0] Read_Data_2
);

  wire Clock_out;

  _32_Bit_Register_File u_32_bit_register_file_1 (
    .Write_Register(Write_Register), .Read_Register_1(Read_Register_1), .Read_Register_2(Read_Register_2),
    .Write_Data(Write_Data), .Reg_Write(Reg_Write), .Clock(Clock_out), .Read_Data_1(Read_Data_1),
    .Read_Data_2(Read_Data_2));
  Clock Clock (.out(Clock_out));
endmodule

module _32_Bit_Register_File (
  input  [4:0] Write_Register,
  input  [4:0] Read_Register_1,
  input  [4:0] Read_Register_2,
  input  Reg_Write,
  input  Clock,
  input  [31:0] Write_Data,
  output [31:0] Read_Data_1,
  output [31:0] Read_Data_2
);

  wire and_1_out, and_2_out, and_3_out, and_4_out, and_5_out, and_6_out, and_7_out, and_8_out, and_9_out,
       and_10_out, and_11_out, and_12_out, and_13_out, and_14_out, and_15_out, and_16_out, and_17_out,
       and_18_out, and_19_out, and_20_out, and_21_out, and_22_out, and_23_out, and_24_out, and_25_out,
       and_26_out, and_27_out, and_28_out, and_29_out, and_30_out, and_31_out, and_32_out, decoder_1_out0,
       decoder_1_out1, decoder_1_out2, decoder_1_out3, decoder_1_out4, decoder_1_out5, decoder_1_out6,
       decoder_1_out7, decoder_1_out8, decoder_1_out9, decoder_1_out10, decoder_1_out11, decoder_1_out12,
       decoder_1_out13, decoder_1_out14, decoder_1_out15, decoder_1_out16, decoder_1_out17, decoder_1_out18,
       decoder_1_out19, decoder_1_out20, decoder_1_out21, decoder_1_out22, decoder_1_out23, decoder_1_out24,
       decoder_1_out25, decoder_1_out26, decoder_1_out27, decoder_1_out28, decoder_1_out29, decoder_1_out30,
       decoder_1_out31;
  wire [31:0] register_1_q, register_2_q, register_3_q, register_4_q, register_5_q, register_6_q,
       register_7_q, register_8_q, register_9_q, register_10_q, register_11_q, register_12_q, register_13_q,
       register_14_q, register_15_q, register_16_q, register_17_q, register_18_q, register_19_q,
       register_20_q, register_21_q, register_22_q, register_23_q, register_24_q, register_25_q,
       register_26_q, register_27_q, register_28_q, register_29_q, register_30_q, register_31_q,
       register_32_q;

  Decoder #(.select(5), .enable("false")) decoder_1 (
    .out0(decoder_1_out0), .out1(decoder_1_out1), .out2(decoder_1_out2), .out3(decoder_1_out3),
    .out4(decoder_1_out4), .out5(decoder_1_out5), .out6(decoder_1_out6), .out7(decoder_1_out7),
    .out8(decoder_1_out8), .out9(decoder_1_out9), .out10(decoder_1_out10), .out11(decoder_1_out11),
    .out12(decoder_1_out12), .out13(decoder_1_out13), .out14(decoder_1_out14), .out15(decoder_1_out15),
    .out16(decoder_1_out16), .out17(decoder_1_out17), .out18(decoder_1_out18), .out19(decoder_1_out19),
    .out20(decoder_1_out20), .out21(decoder_1_out21), .out22(decoder_1_out22), .out23(decoder_1_out23),
    .out24(decoder_1_out24), .out25(decoder_1_out25), .out26(decoder_1_out26), .out27(decoder_1_out27),
    .out28(decoder_1_out28), .out29(decoder_1_out29), .out30(decoder_1_out30), .out31(decoder_1_out31),
    .sel(Write_Register));
  and and_1 (and_1_out, decoder_1_out24, Reg_Write);
  and and_2 (and_2_out, decoder_1_out25, Reg_Write);
  and and_3 (and_3_out, decoder_1_out26, Reg_Write);
  and and_4 (and_4_out, decoder_1_out27, Reg_Write);
  and and_5 (and_5_out, decoder_1_out28, Reg_Write);
  and and_6 (and_6_out, decoder_1_out29, Reg_Write);
  and and_7 (and_7_out, decoder_1_out30, Reg_Write);
  and and_8 (and_8_out, decoder_1_out31, Reg_Write);
  Register #(.width(32)) register_1 (.D(Write_Data), .Q(register_1_q), .clk(Clock), .clr(and_1_out));  // open: en
  Register #(.width(32)) register_2 (.D(Write_Data), .Q(register_2_q), .clk(Clock), .clr(and_2_out));  // open: en
  Register #(.width(32)) register_3 (.D(Write_Data), .Q(register_3_q), .clk(Clock), .clr(and_3_out));  // open: en
  Register #(.width(32)) register_4 (.D(Write_Data), .Q(register_4_q), .clk(Clock), .clr(and_4_out));  // open: en
  Register #(.width(32)) register_5 (.D(Write_Data), .Q(register_5_q), .clk(Clock), .clr(and_5_out));  // open: en
  Register #(.width(32)) register_6 (.D(Write_Data), .Q(register_6_q), .clk(Clock), .clr(and_6_out));  // open: en
  Register #(.width(32)) register_7 (.D(Write_Data), .Q(register_7_q), .clk(Clock), .clr(and_7_out));  // open: en
  Register #(.width(32)) register_8 (.D(Write_Data), .Q(register_8_q), .clk(Clock), .clr(and_8_out));  // open: en
  and and_9 (and_9_out, decoder_1_out16, Reg_Write);
  and and_10 (and_10_out, decoder_1_out17, Reg_Write);
  and and_11 (and_11_out, decoder_1_out18, Reg_Write);
  and and_12 (and_12_out, decoder_1_out19, Reg_Write);
  and and_13 (and_13_out, decoder_1_out20, Reg_Write);
  and and_14 (and_14_out, decoder_1_out21, Reg_Write);
  and and_15 (and_15_out, decoder_1_out22, Reg_Write);
  and and_16 (and_16_out, decoder_1_out23, Reg_Write);
  Register #(.width(32)) register_9 (.D(Write_Data), .Q(register_9_q), .clk(Clock), .clr(and_9_out));  // open: en
  Register #(.width(32)) register_10 (.D(Write_Data), .Q(register_10_q), .clk(Clock), .clr(and_10_out));  // open: en
  Register #(.width(32)) register_11 (.D(Write_Data), .Q(register_11_q), .clk(Clock), .clr(and_11_out));  // open: en
  Register #(.width(32)) register_12 (.D(Write_Data), .Q(register_12_q), .clk(Clock), .clr(and_12_out));  // open: en
  Register #(.width(32)) register_13 (.D(Write_Data), .Q(register_13_q), .clk(Clock), .clr(and_13_out));  // open: en
  Register #(.width(32)) register_14 (.D(Write_Data), .Q(register_14_q), .clk(Clock), .clr(and_14_out));  // open: en
  Register #(.width(32)) register_15 (.D(Write_Data), .Q(register_15_q), .clk(Clock), .clr(and_15_out));  // open: en
  Register #(.width(32)) register_16 (.D(Write_Data), .Q(register_16_q), .clk(Clock), .clr(and_16_out));  // open: en
  and and_17 (and_17_out, decoder_1_out8, Reg_Write);
  and and_18 (and_18_out, decoder_1_out9, Reg_Write);
  and and_19 (and_19_out, decoder_1_out10, Reg_Write);
  and and_20 (and_20_out, decoder_1_out11, Reg_Write);
  and and_21 (and_21_out, decoder_1_out12, Reg_Write);
  and and_22 (and_22_out, decoder_1_out13, Reg_Write);
  and and_23 (and_23_out, decoder_1_out14, Reg_Write);
  and and_24 (and_24_out, decoder_1_out15, Reg_Write);
  Register #(.width(32)) register_17 (.D(Write_Data), .Q(register_17_q), .clk(Clock), .clr(and_17_out));  // open: en
  Register #(.width(32)) register_18 (.D(Write_Data), .Q(register_18_q), .clk(Clock), .clr(and_18_out));  // open: en
  Register #(.width(32)) register_19 (.D(Write_Data), .Q(register_19_q), .clk(Clock), .clr(and_19_out));  // open: en
  Register #(.width(32)) register_20 (.D(Write_Data), .Q(register_20_q), .clk(Clock), .clr(and_20_out));  // open: en
  Register #(.width(32)) register_21 (.D(Write_Data), .Q(register_21_q), .clk(Clock), .clr(and_21_out));  // open: en
  Register #(.width(32)) register_22 (.D(Write_Data), .Q(register_22_q), .clk(Clock), .clr(and_22_out));  // open: en
  Register #(.width(32)) register_23 (.D(Write_Data), .Q(register_23_q), .clk(Clock), .clr(and_23_out));  // open: en
  Register #(.width(32)) register_24 (.D(Write_Data), .Q(register_24_q), .clk(Clock), .clr(and_24_out));  // open: en
  and and_25 (and_25_out, decoder_1_out0, Reg_Write);
  and and_26 (and_26_out, decoder_1_out1, Reg_Write);
  and and_27 (and_27_out, decoder_1_out2, Reg_Write);
  and and_28 (and_28_out, decoder_1_out3, Reg_Write);
  and and_29 (and_29_out, decoder_1_out4, Reg_Write);
  and and_30 (and_30_out, decoder_1_out5, Reg_Write);
  and and_31 (and_31_out, decoder_1_out6, Reg_Write);
  and and_32 (and_32_out, decoder_1_out7, Reg_Write);
  Register #(.width(32)) register_25 (.D(Write_Data), .Q(register_25_q), .clk(Clock), .clr(and_25_out));  // open: en
  Register #(.width(32)) register_26 (.D(Write_Data), .Q(register_26_q), .clk(Clock), .clr(and_26_out));  // open: en
  Register #(.width(32)) register_27 (.D(Write_Data), .Q(register_27_q), .clk(Clock), .clr(and_27_out));  // open: en
  Register #(.width(32)) register_28 (.D(Write_Data), .Q(register_28_q), .clk(Clock), .clr(and_28_out));  // open: en
  Register #(.width(32)) register_29 (.D(Write_Data), .Q(register_29_q), .clk(Clock), .clr(and_29_out));  // open: en
  Register #(.width(32)) register_30 (.D(Write_Data), .Q(register_30_q), .clk(Clock), .clr(and_30_out));  // open: en
  Register #(.width(32)) register_31 (.D(Write_Data), .Q(register_31_q), .clk(Clock), .clr(and_31_out));  // open: en
  Register #(.width(32)) register_32 (.D(Write_Data), .Q(register_32_q), .clk(Clock), .clr(and_32_out));  // open: en
  Multiplexer #(.select(5), .width(32), .enable("false")) multiplexer_1 (
    .in0(register_25_q), .in1(register_26_q), .in2(register_27_q), .in3(register_28_q), .in4(register_29_q),
    .in5(register_30_q), .in6(register_31_q), .in7(register_32_q), .in8(register_17_q), .in9(register_18_q),
    .in10(register_19_q), .in11(register_20_q), .in12(register_21_q), .in13(register_22_q),
    .in14(register_23_q), .in15(register_24_q), .in16(register_9_q), .in17(register_10_q),
    .in18(register_11_q), .in19(register_12_q), .in20(register_13_q), .in21(register_14_q),
    .in22(register_15_q), .in23(register_16_q), .in24(register_1_q), .in25(register_2_q),
    .in26(register_3_q), .in27(register_4_q), .in28(register_5_q), .in29(register_6_q), .in30(register_7_q),
    .in31(register_8_q), .out(Read_Data_1), .sel(Read_Register_1));
  Multiplexer #(.select(5), .width(32), .enable("false")) multiplexer_2 (
    .in0(register_25_q), .in1(register_26_q), .in2(register_27_q), .in3(register_28_q), .in4(register_29_q),
    .in5(register_30_q), .in6(register_31_q), .in7(register_32_q), .in8(register_17_q), .in9(register_18_q),
    .in10(register_19_q), .in11(register_20_q), .in12(register_21_q), .in13(register_22_q),
    .in14(register_23_q), .in15(register_24_q), .in16(register_9_q), .in17(register_10_q),
    .in18(register_11_q), .in19(register_12_q), .in20(register_13_q), .in21(register_14_q),
    .in22(register_15_q), .in23(register_16_q), .in24(register_1_q), .in25(register_2_q),
    .in26(register_3_q), .in27(register_4_q), .in28(register_5_q), .in29(register_6_q), .in30(register_7_q),
    .in31(register_8_q), .out(Read_Data_2), .sel(Read_Register_2));
endmodule
