// Logisim project 32-bit-single-cycle-processor.circ as structural Verilog: 8 circuits, main circuit main
module main (
);

  wire ALU_control_splitter_sub_add_bit, and_1_out, clock_1_out, comparator_1_eq, comparator_2_eq,
       comparator_3_eq, EX_alusrc_2, EX_extop_2, EX_memread_2, EX_memtoreg_2, EX_memwrite_2, EX_regwrite_2,
       Hazard_Forward_stall, main_control_1_alusrc, main_control_1_beq, main_control_1_bne,
       main_control_1_extop, main_control_1_j, main_control_1_memread, main_control_1_memtoreg,
       main_control_1_memwrite, main_control_1_regdst, main_control_1_regwrite, MEM_memread_2,
       MEM_memtoreg_2, MEM_memwrite_2, MEM_regwrite_2, not_1_out, or_1_out, register_2_q, WB_regwrite_2;
  wire [1:0] ALU_control_splitter_alu_selection, ALU_control_splitter_logical_selector, Hazard_Forward_a,
       Hazard_Forward_b, PC_Control_pcsrc;
  wire [2:0] EX_aluop_2, main_control_1_aluop;
  wire [3:0] ALU_control_alu_control;
  wire [4:0] EX_REG_rd2_2, ID_REG_rd, ID_REG_rs, ID_REG_rt, MEM_REG_rd3_2, multiplexer_2_out,
       WB_DATA_RD4_rd4_2;
  wire [5:0] EX_func_2, ID_REG_func, ID_REG_opcode;
  wire [15:0] EX_REG_imm16_2, ID_REG_immediate_16;
  wire [25:0] register_1_q;
  wire [31:0] adder_1_out, adder_2_out, ALU_alu_out, bit_extender_1_out, Data_memory_p7, EX_REG_a_2,
       EX_REG_b_2, EX_REG_npc2_2, extender__32_bit_output, ID_REG_2_npc_2, Instruction_Memory_instruction,
       MEM_REG_aluout_2, MEM_REG_d_2, multiplexer_1_out, multiplexer_3_out, multiplexer_4_out,
       multiplexer_5_out, multiplexer_6_out, multiplier_1_out, Register_File_read_data_1,
       Register_File_read_data_2, WB_DATA_RD4_busw;
  wire [31:2] ID_REG_immediate_26;

  Clock clock_1 (.out(clock_1_out));
  and and_1 (and_1_out, 1'b1, not_1_out);
  not not_1 (not_1_out, Hazard_Forward_stall);
  Multiplexer #(.select(2), .width(32), .disabled(0), .enable("false")) multiplexer_1 (
    .in0(adder_1_out), .in1({ID_REG_immediate_26, 2'b00}), .in2(adder_2_out), .out(multiplexer_1_out),
    .sel(PC_Control_pcsrc));  // open: in3
  Register #(.width(30)) register_1 (
    .D(multiplexer_1_out[31:2]), .en(and_1_out), .Q({ID_REG_immediate_26[31:28], register_1_q}),
    .clk(clock_1_out), .clr(1'b0));
  Comparator #(.width(32)) comparator_1 (
    .a(multiplexer_4_out), .b(multiplexer_3_out), .eq(comparator_1_eq));  // open: gt, lt
  Instruction_Memory Instruction_Memory (
    .address({ID_REG_immediate_26[31:28], register_1_q, 2'b00}), .instruction(Instruction_Memory_instruction));
  pc_control PC_Control (
    .jump(main_control_1_j), .bne(main_control_1_bne), .beq(main_control_1_beq), .zero(comparator_1_eq),
    .PCSrc(PC_Control_pcsrc));
  Comparator #(.width(2)) comparator_2 (.a(2'b10), .b(PC_Control_pcsrc), .eq(comparator_2_eq));  // open: gt, lt
  Adder #(.width(32)) adder_1 (
    .a(32'h4), .b({ID_REG_immediate_26[31:28], register_1_q, 2'b00}), .out(adder_1_out), .cin(1'b0));  // open: cout
  instruction_splitter ID_REG (
    .instruction(Instruction_Memory_instruction), .CLCK(clock_1_out), .opcode(ID_REG_opcode), .rs(ID_REG_rs),
    .rt(ID_REG_rt), .rd(ID_REG_rd), .func(ID_REG_func), .immediate_16(ID_REG_immediate_16),
    .immediate_26(ID_REG_immediate_26[27:2]), .RESET(register_2_q), .ENABLE(and_1_out));  // open: shift_amount
  Register #(.width(1)) register_2 (.D(or_1_out), .en(1'b1), .Q(register_2_q), .clk(clock_1_out), .clr(1'b0));
  or or_1 (or_1_out, comparator_2_eq, comparator_3_eq);
  Comparator #(.width(2)) comparator_3 (.a(2'b01), .b(PC_Control_pcsrc), .eq(comparator_3_eq));  // open: gt, lt
  Multiplexer #(.width(5), .disabled(0), .enable("false")) multiplexer_2 (
    .in0(ID_REG_rt), .in1(ID_REG_rd), .out(multiplexer_2_out), .sel(main_control_1_regdst));
  main_control main_control_1 (
    .opcode(ID_REG_opcode), .RegDst(main_control_1_regdst), .RegWrite(main_control_1_regwrite),
    .ExtOp(main_control_1_extop), .MemRead(main_control_1_memread), .MemWrite(main_control_1_memwrite),
    .MemToReg(main_control_1_memtoreg), .bne(main_control_1_bne), .beq(main_control_1_beq),
    .j(main_control_1_j), .ALUOp(main_control_1_aluop), .ALUSrc(main_control_1_alusrc));
  ID_stage ID_REG_2 (.NPC(adder_1_out), .CLCK(clock_1_out), .NPC_2(ID_REG_2_npc_2));
  _32_Bit_Register_File Register_File (
    .Write_Register(WB_DATA_RD4_rd4_2), .Read_Register_1(ID_REG_rs), .Read_Register_2(ID_REG_rt),
    .Write_Data(WB_DATA_RD4_busw), .Reg_Write(WB_regwrite_2), .Clock(clock_1_out),
    .Read_Data_1(Register_File_read_data_1), .Read_Data_2(Register_File_read_data_2));
  EX EX (
    .RegWrite(main_control_1_regwrite), .ExtOp(main_control_1_extop), .ALUSrc(main_control_1_alusrc),
    .ALUOp(main_control_1_aluop), .func(ID_REG_func), .MemRead(main_control_1_memread),
    .MemWrite(main_control_1_memwrite), .MemToReg(main_control_1_memtoreg), .CLCK(clock_1_out),
    .Stall(Hazard_Forward_stall), .RegWrite_2(EX_regwrite_2), .ExtOp_2(EX_extop_2), .ALUSrc_2(EX_alusrc_2),
    .ALUOp_2(EX_aluop_2), .func_2(EX_func_2), .MemRead_2(EX_memread_2), .MemWrite_2(EX_memwrite_2),
    .MemToReg_2(EX_memtoreg_2));  // open: bne, beq, j, bne_2, beq_2, j_2
  Multiplexer #(.select(2), .width(32), .disabled(0), .enable("false")) multiplexer_3 (
    .in0(Register_File_read_data_1), .in1(ALU_alu_out), .in2(multiplexer_6_out), .in3(WB_DATA_RD4_busw),
    .out(multiplexer_3_out), .sel(Hazard_Forward_a));
  Multiplexer #(.select(2), .width(32), .disabled(0), .enable("false")) multiplexer_4 (
    .in0(Register_File_read_data_2), .in1(ALU_alu_out), .in2(multiplexer_6_out), .in3(WB_DATA_RD4_busw),
    .out(multiplexer_4_out), .sel(Hazard_Forward_b));
  hazard_detect_and_forward Hazard_Forward (
    .rs(ID_REG_rs), .rt(ID_REG_rt), .rd2(EX_REG_rd2_2), .rd3(MEM_REG_rd3_2), .rd4(WB_DATA_RD4_rd4_2),
    .ex_memread(EX_memread_2), .ex_regwrite(EX_regwrite_2), .mem_regwrite(MEM_regwrite_2),
    .wb_regwrite(WB_regwrite_2), .A(Hazard_Forward_a), .B(Hazard_Forward_b), .Stall(Hazard_Forward_stall));
  EX_stage EX_REG (
    .NPC2(ID_REG_2_npc_2), .Imm16(ID_REG_immediate_16), .A(multiplexer_3_out), .B(multiplexer_4_out),
    .RD2(multiplexer_2_out), .CLCK(clock_1_out), .NPC2_2(EX_REG_npc2_2), .Imm16_2(EX_REG_imm16_2),
    .A_2(EX_REG_a_2), .B_2(EX_REG_b_2), .RD2_2(EX_REG_rd2_2));  // open: Imm26, Imm26_2
  assign bit_extender_1_out = {{16{ID_REG_immediate_16[15]}}, ID_REG_immediate_16};  // Bit_Extender bit_extender_1
  Multiplier #(.width(32)) multiplier_1 (
    .a(bit_extender_1_out), .b(32'h4), .out(multiplier_1_out), .cin({32{1'b0}}));  // open: cout
  Adder #(.width(32)) adder_2 (.a(EX_REG_npc2_2), .b(multiplier_1_out), .out(adder_2_out), .cin(1'b0));  // open: cout
  _16to32_bit_extender extender (
    ._16_bit_input(EX_REG_imm16_2), .ext_op(EX_extop_2), ._32_bit_output(extender__32_bit_output));
  Multiplexer #(.width(32), .disabled(0), .enable("false")) multiplexer_5 (
    .in0(EX_REG_b_2), .in1(extender__32_bit_output), .out(multiplexer_5_out), .sel(EX_alusrc_2));
  alu_control_splitter ALU_control_splitter (
    .alu_control(ALU_control_alu_control), .sub_add_bit(ALU_control_splitter_sub_add_bit),
    .alu_selection(ALU_control_splitter_alu_selection),
    .logical_selector(ALU_control_splitter_logical_selector));
  alu_control ALU_control (.func(EX_func_2), .ALUOp(EX_aluop_2), .ALU_Control(ALU_control_alu_control));
  MEM MEM (
    .MemRead(EX_memread_2), .MemWrite(EX_memwrite_2), .MemToReg(EX_memtoreg_2), .CLCK(clock_1_out),
    .RegWrite(EX_regwrite_2), .MemRead_2(MEM_memread_2), .MemWrite_2(MEM_memwrite_2),
    .MemToReg_2(MEM_memtoreg_2), .RegWrite_2(MEM_regwrite_2));
  design_main ALU (
    .shift_operation_selector(2'b11), .A(EX_REG_a_2), .B(multiplexer_5_out),
    .alu_selection(ALU_control_splitter_alu_selection),
    .logical_operation_selector(ALU_control_splitter_logical_selector),
    .sub_add_bit(ALU_control_splitter_sub_add_bit), .alu_out(ALU_alu_out));  // open: carry_out, overflow_flag, zero_flag
  MEM_stage MEM_REG (
    .ALUOut(ALU_alu_out), .D(EX_REG_b_2), .RD3(EX_REG_rd2_2), .CLCK(clock_1_out),
    .ALUOut_2(MEM_REG_aluout_2), .D_2(MEM_REG_d_2), .RD3_2(MEM_REG_rd3_2));
  // _4GB_byte_addressable_memory Data_memory: pin names not known; wires that end beside it: MEM_memwrite_2, MEM_memread_2, MEM_REG_d_2, MEM_REG_aluout_2, 2'b10, clock_1_out, Data_memory_p7
  Multiplexer #(.width(32), .disabled(0), .enable("false")) multiplexer_6 (
    .in0(MEM_REG_aluout_2), .in1(Data_memory_p7), .out(multiplexer_6_out), .sel(MEM_memtoreg_2));
  WB WB (.RegWrite(MEM_regwrite_2), .CLK(clock_1_out), .RegWrite_2(WB_regwrite_2));
  WB_stage WB_DATA_RD4 (
    .WBData(multiplexer_6_out), .RD4(MEM_REG_rd3_2), .CLCK(clock_1_out), .BusW(WB_DATA_RD4_busw),
    .RD4_2(WB_DATA_RD4_rd4_2));
endmodule

module alu_control (
  input  [5:0] func,
  input  [2:0] ALUOp,
  output [3:0] ALU_Control
);

  wire [3:0] bit_extender_1_out, multiplexer_1_out;

  Multiplexer #(.select(4), .width(4)) multiplexer_1 (
    .in0(4'b0100), .in2(4'b0101), .in4(4'b0001), .in5(4'b0010), .in6(4'b0011), .in10(4'b0110),
    .out(multiplexer_1_out), .sel(func[3:0]), .en(1'b1));  // open: in1, in3, in7, in8, in9, in11, in12, in13, in14, in15
  assign bit_extender_1_out = {{1{1'b0}}, ALUOp};  // Bit_Extender bit_extender_1
  Multiplexer #(.select(3), .width(4)) multiplexer_2 (
    .in0(multiplexer_1_out), .in1(bit_extender_1_out), .in2(bit_extender_1_out), .in3(bit_extender_1_out),
    .in4(bit_extender_1_out), .in5(bit_extender_1_out), .in6(bit_extender_1_out), .in7(bit_extender_1_out),
    .out(ALU_Control), .sel(ALUOp), .en(1'b1));
endmodule

module instruction_splitter (
  input  [31:0] instruction,
  input  ENABLE,
  input  RESET,
  input  CLCK,
  output [4:0] shift_amount,
  output [5:0] opcode,
  output [4:0] rs,
  output [4:0] rt,
  output [4:0] rd,
  output [5:0] func,
  output [15:0] immediate_16,
  output [25:0] immediate_26
);

  Register #(.width(5)) register_1 (.D(instruction[10:6]), .en(ENABLE), .Q(shift_amount), .clk(CLCK), .clr(RESET));
  Register #(.width(6)) register_2 (.D(instruction[31:26]), .en(ENABLE), .Q(opcode), .clk(CLCK), .clr(RESET));
  Register #(.width(5)) register_3 (.D(instruction[25:21]), .en(ENABLE), .Q(rs), .clk(CLCK), .clr(RESET));
  Register #(.width(5)) register_4 (.D(instruction[20:16]), .en(ENABLE), .Q(rt), .clk(CLCK), .clr(RESET));
  Register #(.width(5)) register_5 (.D(instruction[15:11]), .en(ENABLE), .Q(rd), .clk(CLCK), .clr(RESET));
  Register #(.width(6)) register_6 (.D(instruction[5:0]), .en(ENABLE), .Q(func), .clk(CLCK), .clr(RESET));
  Register #(.width(16)) register_7 (.D(instruction[15:0]), .en(ENABLE), .Q(immediate_16), .clk(CLCK), .clr(RESET));
  Register #(.width(26)) register_8 (.D(instruction[25:0]), .en(ENABLE), .Q(immediate_26), .clk(CLCK), .clr(RESET));
endmodule

// main control
module main_control (
  input  [5:0] opcode,
  output RegDst,
  output RegWrite,
  output ExtOp,
  output ALUSrc,
  output [2:0] ALUOp,
  output MemRead,
  output MemWrite,
  output MemToReg,
  output bne,
  output beq,
  output j
);

  wire decoder_1_out8, decoder_1_out10, decoder_1_out12, decoder_1_out13, decoder_1_out14, not_1_out;

  not not_1 (not_1_out, opcode[5]);
  Decoder #(.select(5), .disabled(0)) decoder_1 (
    .out0(RegDst), .out2(j), .out4(beq), .out5(bne), .out8(decoder_1_out8), .out10(decoder_1_out10),
    .out12(decoder_1_out12), .out13(decoder_1_out13), .out14(decoder_1_out14), .sel(opcode[4:0]),
    .en(not_1_out));  // open: out1, out3, out6, out7, out9, out11, out15, out16, out17, out18, out19, out20, out21, out22, out23, out24, out25, out26, out27, out28, out29, out30, out31
  Decoder #(.select(5), .disabled(0)) decoder_2 (
    .out3(MemRead), .out11(MemWrite), .sel(opcode[4:0]), .en(opcode[5]));  // open: out0, out1, out2, out4, out5, out6, out7, out8, out9, out10, out12, out13, out14, out15, out16, out17, out18, out19, out20, out21, out22, out23, out24, out25, out26, out27, out28, out29, out30, out31
  nor nor_1 (RegWrite, j, beq, bne, MemWrite);
  nor nor_2 (ExtOp, decoder_1_out12, decoder_1_out13, decoder_1_out14);
  nor nor_3 (ALUSrc, RegDst, beq, bne);
  or or_1 (ALUOp[0], decoder_1_out12, decoder_1_out14, beq, bne);
  or or_2 (ALUOp[1], decoder_1_out13, decoder_1_out14, decoder_1_out10);
  or or_3 (ALUOp[2], decoder_1_out10, decoder_1_out8, MemWrite, MemRead, beq, bne);

  assign MemToReg = MemRead;
endmodule

module alu_control_splitter (
  input  [3:0] alu_control,
  output sub_add_bit,
  output [1:0] alu_selection,
  output [1:0] logical_selector
);

  wire not_1_out, not_2_out;

  not not_1 (not_1_out, alu_control[1]);
  not not_2 (not_2_out, alu_control[2]);
  or or_1 (alu_selection[0], alu_control[1], not_2_out);
  or or_2 (alu_selection[1], not_1_out, not_2_out);
  and and_1 (logical_selector[1], alu_control[1], alu_control[0]);

  assign logical_selector[0] = alu_control[1];
  assign sub_add_bit = alu_control[0];
endmodule

module _16to32_bit_extender (
  input  [15:0] _16_bit_input,
  input  ext_op,
  output [31:0] _32_bit_output
);

  and and_1 (_32_bit_output[31], _16_bit_input[15], ext_op);

  assign _32_bit_output[30:0] = {{15{_32_bit_output[31]}}, _16_bit_input};
endmodule

module pc_control (
  input  jump,
  input  bne,
  input  beq,
  input  zero,
  output [1:0] PCSrc
);

  wire and_1_out, and_2_out, not_1_out;

  not not_1 (not_1_out, zero);
  and and_1 (and_1_out, beq, zero);
  and and_2 (and_2_out, bne, not_1_out);
  or or_1 (PCSrc[1], and_1_out, and_2_out);

  assign PCSrc[0] = jump;
endmodule

module hazard_detect_and_forward (
  input  [4:0] rs,
  input  [4:0] rt,
  input  [4:0] rd2,
  input  [4:0] rd3,
  input  [4:0] rd4,
  input  ex_memread,
  input  ex_regwrite,
  input  mem_regwrite,
  input  wb_regwrite,
  output [1:0] A,
  output [1:0] B,
  output Stall
);

  wire and_1_out, and_2_out, and_3_out, and_4_out, and_5_out, and_6_out, and_7_out, and_8_out,
       comparator_1_eq, comparator_2_eq, comparator_3_eq, comparator_4_eq, comparator_5_eq, comparator_6_eq,
       comparator_7_eq, comparator_8_eq, comparator_9_eq, comparator_10_eq, comparator_11_eq, not_1_out,
       not_2_out, not_3_out, not_4_out, not_5_out, not_6_out, or_1_out, or_2_out, or_5_out;

  Comparator #(.width(5)) comparator_1 (.a(rs), .b({5{1'b0}}), .eq(comparator_1_eq));  // open: gt, lt
  not not_1 (not_1_out, comparator_1_eq);
  Comparator #(.width(5)) comparator_2 (.a(rt), .b({5{1'b0}}), .eq(comparator_2_eq));  // open: gt, lt
  not not_2 (not_2_out, comparator_2_eq);
  Comparator #(.width(5)) comparator_3 (.a(rs), .b(rd2), .eq(comparator_3_eq));  // open: gt, lt
  Comparator #(.width(5)) comparator_4 (.a(rs), .b(rd3), .eq(comparator_4_eq));  // open: gt, lt
  Comparator #(.width(5)) comparator_5 (.a(rs), .b(rd4), .eq(comparator_5_eq));  // open: gt, lt
  Comparator #(.width(5)) comparator_6 (.a(rt), .b(rd2), .eq(comparator_6_eq));  // open: gt, lt
  Comparator #(.width(5)) comparator_7 (.a(rt), .b(rd3), .eq(comparator_7_eq));  // open: gt, lt
  Comparator #(.width(5)) comparator_8 (.a(rt), .b(rd4), .eq(comparator_8_eq));  // open: gt, lt
  Comparator #(.width(1)) comparator_9 (.a(1'b1), .b(ex_memread), .eq(comparator_9_eq));  // open: gt, lt
  and and_1 (and_1_out, not_1_out, comparator_3_eq, ex_regwrite);
  and and_2 (and_2_out, not_1_out, comparator_4_eq, mem_regwrite);
  and and_3 (and_3_out, not_1_out, comparator_5_eq, wb_regwrite);
  and and_4 (and_4_out, not_2_out, comparator_6_eq, ex_regwrite);
  and and_5 (and_5_out, not_2_out, comparator_7_eq, mem_regwrite);
  and and_6 (and_6_out, not_2_out, comparator_8_eq, wb_regwrite);
  or or_1 (or_1_out, and_2_out, and_3_out);
  not not_3 (not_3_out, and_2_out);
  and and_7 (and_7_out, not_3_out, and_3_out);
  or or_2 (or_2_out, and_5_out, and_6_out);
  not not_4 (not_4_out, and_5_out);
  and and_8 (and_8_out, not_4_out, and_6_out);
  not not_5 (not_5_out, and_1_out);
  and and_9 (A[1], not_5_out, or_1_out);
  or or_3 (A[0], and_1_out, and_7_out);
  not not_6 (not_6_out, and_4_out);
  and and_10 (B[1], not_6_out, or_2_out);
  or or_4 (B[0], and_4_out, and_8_out);
  Comparator #(.width(2)) comparator_10 (.a(A), .b(2'b01), .eq(comparator_10_eq));  // open: gt, lt
  Comparator #(.width(2)) comparator_11 (.a(B), .b(2'b01), .eq(comparator_11_eq));  // open: gt, lt
  or or_5 (or_5_out, comparator_10_eq, comparator_11_eq);
  and and_11 (Stall, comparator_9_eq, or_5_out);
endmodule
