// Logisim project 4GB byte-addressable memory.circ as structural Verilog: 4 circuits, main circuit main
module _29 (
  input  read_write,
  input  [31:0] datain,
  input  [28:0] address,
  input  [1:0] byte_half_word,
  input  clock,
  output [31:0] dataout
);

  wire demultiplexer_1_out0, demultiplexer_1_out1, demultiplexer_1_out2, demultiplexer_1_out3,
       demultiplexer_1_out4, demultiplexer_1_out5, demultiplexer_1_out6, demultiplexer_1_out7;
  wire [31:0] n26_1_dataout, n26_2_dataout, n26_3_dataout, n26_4_dataout, n26_5_dataout, n26_6_dataout,
       n26_7_dataout, n26_8_dataout;

  Demultiplexer #(.select(3), .enable("false")) demultiplexer_1 (
    .out0(demultiplexer_1_out0), .out1(demultiplexer_1_out1), .out2(demultiplexer_1_out2),
    .out3(demultiplexer_1_out3), .out4(demultiplexer_1_out4), .out5(demultiplexer_1_out5),
    .out6(demultiplexer_1_out6), .out7(demultiplexer_1_out7), .in(clock), .sel(address[28:26]));
  _26 u_26_1 (
    .address(address[25:0]), .Read_Write(read_write), .datain(datain), .byte_half_word(byte_half_word),
    .clock(demultiplexer_1_out0), .dataout(n26_1_dataout));
  _26 u_26_2 (
    .address(address[25:0]), .Read_Write(read_write), .datain(datain), .byte_half_word(byte_half_word),
    .clock(demultiplexer_1_out1), .dataout(n26_2_dataout));
  _26 u_26_3 (
    .address(address[25:0]), .Read_Write(read_write), .datain(datain), .byte_half_word(byte_half_word),
    .clock(demultiplexer_1_out2), .dataout(n26_3_dataout));
  _26 u_26_4 (
    .address(address[25:0]), .Read_Write(read_write), .datain(datain), .byte_half_word(byte_half_word),
    .clock(demultiplexer_1_out3), .dataout(n26_4_dataout));
  _26 u_26_5 (
    .address(address[25:0]), .Read_Write(read_write), .datain(datain), .byte_half_word(byte_half_word),
    .clock(demultiplexer_1_out4), .dataout(n26_5_dataout));
  Multiplexer #(.select(3), .width(32), .enable("false")) multiplexer_1 (
    .in0(n26_1_dataout), .in1(n26_2_dataout), .in2(n26_3_dataout), .in3(n26_4_dataout), .in4(n26_5_dataout),
    .in5(n26_6_dataout), .in6(n26_7_dataout), .in7(n26_8_dataout), .out(dataout), .sel(address[28:26]));
  _26 u_26_6 (
    .address(address[25:0]), .Read_Write(read_write), .datain(datain), .byte_half_word(byte_half_word),
    .clock(demultiplexer_1_out5), .dataout(n26_6_dataout));
  _26 u_26_7 (
    .address(address[25:0]), .Read_Write(read_write), .datain(datain), .byte_half_word(byte_half_word),
    .clock(demultiplexer_1_out6), .dataout(n26_7_dataout));
  _26 u_26_8 (
    .address(address[25:0]), .Read_Write(read_write), .datain(datain), .byte_half_word(byte_half_word),
    .clock(demultiplexer_1_out7), .dataout(n26_8_dataout));
endmodule

module _26 (
  input  [25:0] address,
  input  Read_Write,
  input  [31:0] datain,
  input  [1:0] byte_half_word,
  input  clock,
  output [31:0] dataout
);

  wire and_1_out, and_2_out, and_3_out, and_4_out, and_5_out, and_6_out, and_7_out, and_8_out, and_9_out,
       and_10_out, and_11_out, and_12_out, byte_out, half_out, not_1_out, not_2_out, not_3_out, not_4_out,
       not_5_out, not_6_out, not_7_out, not_8_out, not_9_out, not_10_out, not_11_out, not_12_out, not_13_out,
       or_1_out, or_2_out, or_3_out, or_4_out, word_out;

  and \byte  (byte_out, not_1_out, not_6_out);
  not not_1 (not_1_out, byte_half_word[1]);
  not not_2 (not_2_out, address[0]);
  not not_3 (not_3_out, address[1]);
  not not_4 (not_4_out, address[1]);
  and and_1 (and_1_out, not_3_out, not_2_out);
  and half (half_out, not_5_out, byte_half_word[0]);
  not not_5 (not_5_out, byte_half_word[1]);
  not not_6 (not_6_out, byte_half_word[0]);
  not not_7 (not_7_out, address[0]);
  and and_2 (and_2_out, address[1], not_7_out);
  and and_3 (and_3_out, not_4_out, address[0]);
  and word (word_out, byte_half_word[1], not_8_out);
  not not_8 (not_8_out, byte_half_word[0]);
  and and_4 (and_4_out, address[0], address[1]);
  not not_9 (not_9_out, address[1]);
  and and_5 (and_5_out, and_1_out, byte_out);
  and and_6 (and_6_out, and_3_out, byte_out);
  and and_7 (and_7_out, and_2_out, byte_out);
  and and_8 (and_8_out, and_4_out, byte_out);
  and and_9 (and_9_out, not_9_out, half_out);
  and and_10 (and_10_out, not_9_out, half_out);
  and and_11 (and_11_out, address[1], half_out);
  and and_12 (and_12_out, address[1], half_out);
  or or_1 (or_1_out, word_out, and_9_out, and_5_out);
  or or_2 (or_2_out, word_out, and_10_out, and_6_out);
  or or_3 (or_3_out, word_out, and_11_out, and_7_out);
  or or_4 (or_4_out, word_out, and_12_out, and_8_out);
  not not_10 (not_10_out, Read_Write);
  not not_11 (not_11_out, Read_Write);
  not not_12 (not_12_out, Read_Write);
  not not_13 (not_13_out, Read_Write);
  RAM #(.addrWidth(24), .bus("separate")) ram_1 (
    .addr(address[25:2]), .din(datain[7:0]), .data(dataout[7:0]), .str(Read_Write), .sel(or_1_out),
    .clk(clock), .ld(not_10_out));  // open: clr
  RAM #(.addrWidth(24), .bus("separate")) ram_2 (
    .addr(address[25:2]), .din(datain[15:8]), .data(dataout[15:8]), .str(Read_Write), .sel(or_2_out),
    .clk(clock), .ld(not_11_out));  // open: clr
  RAM #(.addrWidth(24), .bus("separate")) ram_3 (
    .addr(address[25:2]), .din(datain[23:16]), .data(dataout[23:16]), .str(Read_Write), .sel(or_3_out),
    .clk(clock), .ld(not_12_out));  // open: clr
  RAM #(.addrWidth(24), .bus("separate")) ram_4 (
    .addr(address[25:2]), .din(datain[31:24]), .data(dataout[31:24]), .str(Read_Write), .sel(or_4_out),
    .clk(clock), .ld(not_13_out));  // open: clr

  // Notes on the sheet:
  //   Byte 0
  //   Byte 1
  //   Byte 2
  //   Byte 3
endmodule

module _4GB_byte_addressable_memory (
  input  read_write,
  input  [31:0] datain,
  input  [31:0] address,
  input  [1:0] byte_half_word,
  input  clock,
  output [31:0] dataout
);

  wire demultiplexer_1_out0, demultiplexer_1_out1, demultiplexer_1_out2, demultiplexer_1_out3,
       demultiplexer_1_out4, demultiplexer_1_out5, demultiplexer_1_out6, demultiplexer_1_out7;
  wire [31:0] n29_1_dataout, n29_2_dataout, n29_3_dataout, n29_4_dataout, n29_5_dataout, n29_6_dataout,
       n29_7_dataout, n29_8_dataout;

  Demultiplexer #(.select(3), .enable("false")) demultiplexer_1 (
    .out0(demultiplexer_1_out0), .out1(demultiplexer_1_out1), .out2(demultiplexer_1_out2),
    .out3(demultiplexer_1_out3), .out4(demultiplexer_1_out4), .out5(demultiplexer_1_out5),
    .out6(demultiplexer_1_out6), .out7(demultiplexer_1_out7), .in(clock), .sel(address[31:29]));
  _29 u_29_1 (
    .read_write(read_write), .datain(datain), .address(address[28:0]), .byte_half_word(byte_half_word),
    .clock(demultiplexer_1_out0), .dataout(n29_1_dataout));
  _29 u_29_2 (
    .read_write(read_write), .datain(datain), .address(address[28:0]), .byte_half_word(byte_half_word),
    .clock(demultiplexer_1_out1), .dataout(n29_2_dataout));
  _29 u_29_3 (
    .read_write(read_write), .datain(datain), .address(address[28:0]), .byte_half_word(byte_half_word),
    .clock(demultiplexer_1_out2), .dataout(n29_3_dataout));
  _29 u_29_4 (
    .read_write(read_write), .datain(datain), .address(address[28:0]), .byte_half_word(byte_half_word),
    .clock(demultiplexer_1_out3), .dataout(n29_4_dataout));
  _29 u_29_5 (
    .read_write(read_write), .datain(datain), .address(address[28:0]), .byte_half_word(byte_half_word),
    .clock(demultiplexer_1_out4), .dataout(n29_5_dataout));
  Multiplexer #(.select(3), .width(32), .enable("false")) multiplexer_1 (
    .in0(n29_1_dataout), .in1(n29_2_dataout), .in2(n29_3_dataout), .in3(n29_4_dataout), .in4(n29_5_dataout),
    .in5(n29_6_dataout), .in6(n29_7_dataout), .in7(n29_8_dataout), .out(dataout), .sel(address[31:29]));
  _29 u_29_6 (
    .read_write(read_write), .datain(datain), .address(address[28:0]), .byte_half_word(byte_half_word),
    .clock(demultiplexer_1_out5), .dataout(n29_6_dataout));
  _29 u_29_7 (
    .read_write(read_write), .datain(datain), .address(address[28:0]), .byte_half_word(byte_half_word),
    .clock(demultiplexer_1_out6), .dataout(n29_7_dataout));
  _29 u_29_8 (
    .read_write(read_write), .datain(datain), .address(address[28:0]), .byte_half_word(byte_half_word),
    .clock(demultiplexer_1_out7), .dataout(n29_8_dataout));
endmodule

module main (
  input  read_write,
  input  [31:0] datain,
  input  [31:0] addresss,
  input  [1:0] byte_half_word,
  output [31:0] out_5
);

  wire clock_1_out;

  Clock clock_1 (.out(clock_1_out));
  _4GB_byte_addressable_memory u_4gb_byte_addressable_memory_1 (
    .read_write(read_write), .datain(datain), .address(addresss), .byte_half_word(byte_half_word),
    .dataout(out_5), .clock(clock_1_out));
endmodule
