// Logisim project Arithmetic Unit.circ as structural Verilog: 2 circuits, main circuit Full Adder
// FA
module Full_Adder (
  input  Cin,
  input  A,
  input  B,
  output S,
  output Cout
);

  wire and_1_out, and_2_out, xor_1_out;

  xor xor_1 (xor_1_out, A, B);
  xor xor_2 (S, xor_1_out, Cin);
  and and_1 (and_1_out, Cin, xor_1_out);
  and and_2 (and_2_out, B, A);
  xor xor_3 (Cout, and_1_out, and_2_out);
endmodule

module Ripple_Adder (
  input  ADD_SUB,
  input  [31:0] A,
  input  [31:0] B,
  output [31:0] F,
  output Cout,
  output Overflow
);

  wire _0_2_cout, _0_out, _1_2_cout, _1_out, _2_2_cout, _2_out, _3_2_cout, _3_out, _4_2_cout, _4_out,
       _5_2_cout, _5_out, _6_2_cout, _6_out, _7_2_cout, _7_out, _8_2_cout, _8_out, _9_2_cout, _9_out,
       _10_2_cout, _10_out, _11_2_cout, _11_out, _12_2_cout, _12_out, _13_2_cout, _13_out, _14_2_cout,
       _14_out, _15_2_cout, _15_out, _16_2_cout, _16_out, _17_2_cout, _17_out, _18_2_cout, _18_out,
       _19_2_cout, _19_out, _20_2_cout, _20_out, _21_2_cout, _21_out, _22_2_cout, _22_out, _23_2_cout,
       _23_out, _24_2_cout, _24_out, _25_2_cout, _25_out, _26_2_cout, _26_out, _27_2_cout, _27_out,
       _28_2_cout, _28_out, _29_2_cout, _29_out, _30_out, _31_out;

  xor _0 (_0_out, B[0], ADD_SUB);
  xor _1 (_1_out, B[1], ADD_SUB);
  xor _2 (_2_out, B[2], ADD_SUB);
  xor _3 (_3_out, B[3], ADD_SUB);
  xor _4 (_4_out, B[4], ADD_SUB);
  xor _5 (_5_out, B[5], ADD_SUB);
  xor _6 (_6_out, B[6], ADD_SUB);
  xor _7 (_7_out, B[7], ADD_SUB);
  xor _8 (_8_out, B[9], ADD_SUB);
  xor _9 (_9_out, B[9], ADD_SUB);
  xor _10 (_10_out, B[10], ADD_SUB);
  xor _11 (_11_out, B[11], ADD_SUB);
  xor _12 (_12_out, B[12], ADD_SUB);
  xor _13 (_13_out, B[13], ADD_SUB);
  xor _14 (_14_out, B[14], ADD_SUB);
  xor _15 (_15_out, B[15], ADD_SUB);
  Full_Adder _0_2 (.Cin(ADD_SUB), .A(A[0]), .B(_0_out), .S(F[0]), .Cout(_0_2_cout));
  Full_Adder _1_2 (.Cin(_0_2_cout), .A(A[1]), .B(_1_out), .S(F[1]), .Cout(_1_2_cout));
  Full_Adder _2_2 (.Cin(_1_2_cout), .A(A[2]), .B(_2_out), .S(F[2]), .Cout(_2_2_cout));
  Full_Adder _3_2 (.Cin(_2_2_cout), .A(A[3]), .B(_3_out), .S(F[3]), .Cout(_3_2_cout));
  Full_Adder _4_2 (.Cin(_3_2_cout), .A(A[4]), .B(_4_out), .S(F[4]), .Cout(_4_2_cout));
  Full_Adder _5_2 (.Cin(_4_2_cout), .A(A[5]), .B(_5_out), .S(F[5]), .Cout(_5_2_cout));
  Full_Adder _6_2 (.Cin(_5_2_cout), .A(A[6]), .B(_6_out), .S(F[6]), .Cout(_6_2_cout));
  Full_Adder _7_2 (.Cin(_6_2_cout), .A(A[7]), .B(_7_out), .S(F[7]), .Cout(_7_2_cout));
  Full_Adder _8_2 (.Cin(_7_2_cout), .A(A[8]), .B(_8_out), .S(F[8]), .Cout(_8_2_cout));
  Full_Adder _9_2 (.Cin(_8_2_cout), .A(A[9]), .B(_9_out), .S(F[9]), .Cout(_9_2_cout));
  Full_Adder _10_2 (.Cin(_9_2_cout), .A(A[10]), .B(_10_out), .S(F[10]), .Cout(_10_2_cout));
  Full_Adder _11_2 (.Cin(_10_2_cout), .A(A[11]), .B(_11_out), .S(F[11]), .Cout(_11_2_cout));
  Full_Adder _12_2 (.Cin(_11_2_cout), .A(A[12]), .B(_12_out), .S(F[12]), .Cout(_12_2_cout));
  Full_Adder _13_2 (.Cin(_12_2_cout), .A(A[13]), .B(_13_out), .S(F[13]), .Cout(_13_2_cout));
  Full_Adder _14_2 (.Cin(_13_2_cout), .A(A[14]), .B(_14_out), .S(F[14]), .Cout(_14_2_cout));
  Full_Adder _15_2 (.Cin(_14_2_cout), .A(A[15]), .B(_15_out), .S(F[15]), .Cout(_15_2_cout));
  xor _16 (_16_out, B[16], ADD_SUB);
  xor _17 (_17_out, B[17], ADD_SUB);
  xor _18 (_18_out, B[18], ADD_SUB);
  xor _19 (_19_out, B[19], ADD_SUB);
  xor _20 (_20_out, B[20], ADD_SUB);
  xor _21 (_21_out, B[21], ADD_SUB);
  xor _22 (_22_out, B[22], ADD_SUB);
  xor _23 (_23_out, B[23], ADD_SUB);
  xor _24 (_24_out, B[24], ADD_SUB);
  xor _25 (_25_out, B[25], ADD_SUB);
  xor _26 (_26_out, B[26], ADD_SUB);
  xor _27 (_27_out, B[27], ADD_SUB);
  xor _28 (_28_out, B[28], ADD_SUB);
  xor _29 (_29_out, B[29], ADD_SUB);
  xor _30 (_30_out, B[30], ADD_SUB);
  xor _31 (_31_out, B[31], ADD_SUB);
  Full_Adder _16_2 (.Cin(_15_2_cout), .A(A[16]), .B(_16_out), .S(F[16]), .Cout(_16_2_cout));
  Full_Adder _17_2 (.Cin(_16_2_cout), .A(A[17]), .B(_17_out), .S(F[17]), .Cout(_17_2_cout));
  Full_Adder _18_2 (.Cin(_17_2_cout), .A(A[18]), .B(_18_out), .S(F[18]), .Cout(_18_2_cout));
  Full_Adder _19_2 (.Cin(_18_2_cout), .A(A[19]), .B(_19_out), .S(F[19]), .Cout(_19_2_cout));
  Full_Adder _20_2 (.Cin(_19_2_cout), .A(A[20]), .B(_20_out), .S(F[20]), .Cout(_20_2_cout));
  Full_Adder _21_2 (.Cin(_20_2_cout), .A(A[21]), .B(_21_out), .S(F[21]), .Cout(_21_2_cout));
  Full_Adder _22_2 (.Cin(_21_2_cout), .A(A[22]), .B(_22_out), .S(F[22]), .Cout(_22_2_cout));
  Full_Adder _23_2 (.Cin(_22_2_cout), .A(A[23]), .B(_23_out), .S(F[23]), .Cout(_23_2_cout));
  Full_Adder _24_2 (.Cin(_23_2_cout), .A(A[24]), .B(_24_out), .S(F[24]), .Cout(_24_2_cout));
  Full_Adder _25_2 (.Cin(_24_2_cout), .A(A[25]), .B(_25_out), .S(F[25]), .Cout(_25_2_cout));
  Full_Adder _26_2 (.Cin(_25_2_cout), .A(A[26]), .B(_26_out), .S(F[26]), .Cout(_26_2_cout));
  Full_Adder _27_2 (.Cin(_26_2_cout), .A(A[27]), .B(_27_out), .S(F[27]), .Cout(_27_2_cout));
  Full_Adder _28_2 (.Cin(_27_2_cout), .A(A[28]), .B(_28_out), .S(F[28]), .Cout(_28_2_cout));
  Full_Adder _29_2 (.Cin(_28_2_cout), .A(A[29]), .B(_29_out), .S(F[29]), .Cout(_29_2_cout));
  Full_Adder _30_2 (.Cin(_29_2_cout), .A(A[30]), .B(_30_out), .S(F[30]), .Cout(A[31]));
  Full_Adder _31_2 (.Cin(A[31]), .A(A[31]), .B(_31_out), .S(F[31]), .Cout(Cout));
  xor xor_1 (Overflow, Cout, A[31]);

  assign B[8] = B[9];
endmodule
