// Logisim project Instruction memory.circ as structural Verilog: 5 circuits, main circuit 28
module _26 (
  input  [25:0] address,
  output [31:0] instruction
);

  wire [31:0] rom_1_data, rom_2_data, rom_3_data, rom_4_data;

  ROM #(.addrWidth(24), .dataWidth(32)) rom_1 (.addr(address[23:0]), .data(rom_1_data));  // open: sel
  ROM #(.addrWidth(24), .dataWidth(32)) rom_2 (.addr(address[23:0]), .data(rom_2_data));  // open: sel
  ROM #(.addrWidth(24), .dataWidth(32)) rom_3 (.addr(address[23:0]), .data(rom_3_data));  // open: sel
  ROM #(.addrWidth(24), .dataWidth(32)) rom_4 (.addr(address[23:0]), .data(rom_4_data));  // open: sel
  Multiplexer #(.select(2), .width(32), .enable("false")) multiplexer_1 (
    .in0(rom_1_data), .in1(rom_2_data), .in2(rom_3_data), .in3(rom_4_data), .out(instruction),
    .sel(address[25:24]));
endmodule

module _28 (
  input  [27:0] address,
  output [31:0] instruction
);

  wire [31:0] n26_1_instruction, n26_2_instruction, n26_3_instruction, n26_4_instruction;

  _26 u_26_1 (.address(address[25:0]), .instruction(n26_1_instruction));
  _26 u_26_2 (.address(address[25:0]), .instruction(n26_2_instruction));
  _26 u_26_3 (.address(address[25:0]), .instruction(n26_3_instruction));
  _26 u_26_4 (.address(address[25:0]), .instruction(n26_4_instruction));
  Multiplexer #(.select(2), .width(32), .enable("false")) multiplexer_1 (
    .in0(n26_1_instruction), .in1(n26_2_instruction), .in2(n26_3_instruction), .in3(n26_4_instruction),
    .out(instruction), .sel(address[27:26]));
endmodule

module _30 (
  input  [29:0] address,
  output [31:0] dataout
);

  wire [31:0] n28_1_instruction, n28_2_instruction, n28_3_instruction, n28_4_instruction;

  _28 u_28_1 (.address(address[27:0]), .instruction(n28_1_instruction));
  _28 u_28_2 (.address(address[27:0]), .instruction(n28_2_instruction));
  _28 u_28_3 (.address(address[27:0]), .instruction(n28_3_instruction));
  _28 u_28_4 (.address(address[27:0]), .instruction(n28_4_instruction));
  Multiplexer #(.select(2), .width(32), .enable("false")) multiplexer_1 (
    .in0(n28_1_instruction), .in1(n28_2_instruction), .in2(n28_3_instruction), .in3(n28_4_instruction),
    .out(dataout), .sel(address[29:28]));
endmodule

module _32 (
  input  [31:0] address,
  output [31:0] instruction
);

  wire [31:0] n30_1_dataout, n30_2_dataout, n30_3_dataout, n30_4_dataout;

  _30 u_30_1 (.address(address[29:0]), .dataout(n30_1_dataout));
  _30 u_30_2 (.address(address[29:0]), .dataout(n30_2_dataout));
  _30 u_30_3 (.address(address[29:0]), .dataout(n30_3_dataout));
  _30 u_30_4 (.address(address[29:0]), .dataout(n30_4_dataout));
  Multiplexer #(.select(2), .width(32), .enable("false")) multiplexer_1 (
    .in0(n30_1_dataout), .in1(n30_2_dataout), .in2(n30_3_dataout), .in3(n30_4_dataout), .out(instruction),
    .sel(address[31:30]));
endmodule

module Instruction_Memory (
  input  [31:0] address,
  output [31:0] instruction
);

  _32 u_32_1 (.address(address), .instruction(instruction));
endmodule
