// Logisim project design.circ as structural Verilog: 8 circuits, main circuit main
module main (
  input  [1:0] shift_operation_selector,
  input  [31:0] A,
  input  [31:0] B,
  input  sub_add_bit,
  input  [1:0] alu_selection,
  input  [1:0] logical_operation_selector,
  output carry_out,
  output overflow_flag,
  output [31:0] alu_out,
  output zero_flag
);

  wire and_1_out, not_1_out, or_1_out;
  wire [4:0] bit_extender_1_out;
  wire [31:0] comparator_1_a_2, logic_block_out, ripple_adder_1_f, shifter_block_data_out;

  Bit_Extender #(.in_width(32), .out_width(5)) bit_extender_1 (.in(A), .out(bit_extender_1_out));
  shifter shifter_block (
    ._32_bit_input(B), .shift_amount(bit_extender_1_out), .data_out(shifter_block_data_out),
    .shift_op(shift_operation_selector));
  ripple_adder ripple_adder_1 (
    .ADD_SUB(or_1_out), .A(A), .B(B), .F(ripple_adder_1_f), .Cout(carry_out), .Overflow(overflow_flag));
  or or_1 (or_1_out, sub_add_bit, and_1_out);
  and and_1 (and_1_out, not_1_out, alu_selection[0]);
  not not_1 (not_1_out, alu_selection[1]);
  logical_operations logic_block (.A(A), .B(B), .selector(logical_operation_selector), .out(logic_block_out));
  comparator comparator_1 (
    .A(A), .B(A), .adder_result(ripple_adder_1_f), .overflow(overflow_flag), .cout(carry_out),
    .A_2(comparator_1_a_2));
  Multiplexer #(.select(2), .width(32)) multiplexer_1 (
    .in0(shifter_block_data_out), .in1(comparator_1_a_2), .in2(ripple_adder_1_f), .in3(logic_block_out),
    .out(alu_out), .sel(alu_selection), .en(1'b1));
  zero_detector zero_detector_1 (._32_bit_Input(alu_out), .zero_bit_flag(zero_flag));
endmodule

module logical_operations (
  input  [31:0] A,
  input  [31:0] B,
  input  [1:0] selector,
  output [31:0] out
);

  wire [31:0] and_1_out, not_1_out, or_1_out, xor_1_out;

  assign and_1_out = A & B;  // AND_Gate and_1, 32 bits wide
  assign or_1_out = A | B;  // OR_Gate or_1, 32 bits wide
  assign xor_1_out = A ^ B;  // XOR_Gate xor_1, 32 bits wide
  assign not_1_out = ~or_1_out;  // NOT_Gate not_1, 32 bits wide
  Multiplexer #(.select(2), .width(32)) multiplexer_1 (
    .in0(and_1_out), .in1(or_1_out), .in2(not_1_out), .in3(xor_1_out), .out(out), .sel(selector), .en(1'b1));
endmodule

module zero_detector (
  input  [31:0] _32_bit_Input,
  output zero_bit_flag
);

  nor nor_1 (zero_bit_flag, _32_bit_Input[0], _32_bit_Input[1], _32_bit_Input[2], _32_bit_Input[3], _32_bit_Input[4], _32_bit_Input[5], _32_bit_Input[6], _32_bit_Input[7], _32_bit_Input[8], _32_bit_Input[9], _32_bit_Input[10], _32_bit_Input[11], _32_bit_Input[12], _32_bit_Input[13], _32_bit_Input[14], _32_bit_Input[15], _32_bit_Input[17], _32_bit_Input[18], _32_bit_Input[19], _32_bit_Input[20], _32_bit_Input[21], _32_bit_Input[22], _32_bit_Input[23], _32_bit_Input[24], _32_bit_Input[25], _32_bit_Input[26], _32_bit_Input[27], _32_bit_Input[28], _32_bit_Input[29], _32_bit_Input[30], _32_bit_Input[31], _32_bit_Input[16]);
endmodule

module shifter (
  input  [31:0] _32_bit_input,
  input  [1:0] shift_op,
  input  [4:0] shift_amount,
  output [31:0] data_out
);

  wire and_1_out, xor_1_out, xor_2_out, xor_3_out, xor_4_out, xor_5_out;
  wire [2:0] multiplexer_6_out;
  wire [3:0] multiplexer_3_out;
  wire [6:0] multiplexer_4_out;
  wire [14:0] multiplexer_2_out;
  wire [27:0] multiplexer_3_out_2;
  wire [30:0] extender__63_32;
  wire [31:0] extender__31_0, multiplexer_1_out, multiplexer_5_out, multiplexer_7_out;
  wire [31:31] multiplexer_8_out;

  xor xor_1 (xor_1_out, shift_amount[4], and_1_out);
  xor xor_2 (xor_2_out, shift_amount[3], and_1_out);
  xor xor_3 (xor_3_out, shift_amount[2], and_1_out);
  xor xor_4 (xor_4_out, shift_amount[1], and_1_out);
  shifter_extender_63_bit extender (
    ._32_bit_input(_32_bit_input), .shift_op(shift_op), ._31_0(extender__31_0), ._63_32(extender__63_32));
  and and_1 (and_1_out, shift_op[1], shift_op[0]);
  xor xor_5 (xor_5_out, shift_amount[0], and_1_out);
  Multiplexer #(.width(32)) multiplexer_1 (
    .in0(extender__31_0), .in1({extender__63_32[15:0], extender__31_0[31:16]}), .out(multiplexer_1_out),
    .sel(xor_1_out), .en(1'b1));
  Multiplexer #(.width(15)) multiplexer_2 (
    .in0(extender__63_32[14:0]), .in1(extender__63_32[30:16]), .out(multiplexer_2_out), .sel(xor_1_out),
    .en(1'b1));
  Multiplexer #(.width(32)) multiplexer_3 (
    .in0(multiplexer_1_out), .in1({multiplexer_2_out[7:0], multiplexer_1_out[31:8]}),
    .out({multiplexer_3_out_2, multiplexer_3_out}), .sel(xor_2_out), .en(1'b1));
  Multiplexer #(.width(7)) multiplexer_4 (
    .in0(multiplexer_2_out[6:0]), .in1(multiplexer_2_out[14:8]), .out(multiplexer_4_out), .sel(xor_2_out),
    .en(1'b1));
  Multiplexer #(.width(32)) multiplexer_5 (
    .in0({multiplexer_3_out_2, multiplexer_3_out}), .in1({multiplexer_4_out[3:0], multiplexer_3_out_2}),
    .out(multiplexer_5_out), .sel(xor_3_out), .en(1'b1));
  Multiplexer #(.width(3)) multiplexer_6 (
    .in0(multiplexer_4_out[2:0]), .in1(multiplexer_4_out[6:4]), .out(multiplexer_6_out), .sel(xor_3_out),
    .en(1'b1));
  Multiplexer #(.width(32)) multiplexer_7 (
    .in0(multiplexer_5_out), .in1({multiplexer_6_out[1:0], multiplexer_5_out[31:2]}),
    .out(multiplexer_7_out), .sel(xor_4_out), .en(1'b1));
  Multiplexer multiplexer_8 (
    .in0(multiplexer_6_out[0]), .in1(multiplexer_6_out[2]), .out(multiplexer_8_out[31]), .sel(xor_4_out),
    .en(1'b1));
  Multiplexer #(.width(32)) multiplexer_9 (
    .in0(multiplexer_7_out), .in1({multiplexer_8_out[31], multiplexer_7_out[31:1]}), .out(data_out),
    .sel(xor_5_out), .en(1'b1));

  // Notes on the sheet:
  //   [31:0]
  //   [47:32]
  //   [31:0]
  //   [39:32]
  //   [31:0]
  //   [34:32]
  //   [31:0]
  //   [32]
endmodule

module shifter_extender_63_bit (
  input  [31:0] _32_bit_input,
  input  [1:0] shift_op,
  output [31:0] _31_0,
  output [30:0] _63_32
);

  wire [30:0] bit_extender_1_out, bit_extender_2_out;

  assign bit_extender_1_out = {{30{1'b0}}, 1'b0};  // Bit_Extender bit_extender_1
  assign bit_extender_2_out = {{30{_32_bit_input[31]}}, _32_bit_input[31]};  // Bit_Extender bit_extender_2
  Multiplexer #(.select(2), .width(31)) multiplexer_1 (
    .in0(bit_extender_1_out), .in1(bit_extender_2_out), .in2(_32_bit_input[30:0]), .in3(_32_bit_input[31:1]),
    .out(_63_32), .sel(shift_op), .en(1'b1));
  Multiplexer #(.select(2), .width(32)) multiplexer_2 (
    .in0(_32_bit_input), .in1(_32_bit_input), .in2(_32_bit_input),
    .in3({_32_bit_input[0], bit_extender_1_out}), .out(_31_0), .sel(shift_op), .en(1'b1));
endmodule

module ripple_adder (
  input  ADD_SUB,
  input  [31:0] A,
  input  [31:0] B,
  output [31:0] F,
  output Cout,
  output Overflow
);

  wire _0_2_cout, _0_out, _1_2_cout, _1_out, _2_2_cout, _2_out, _3_2_cout, _3_out, _4_2_cout, _4_out,
       _5_2_cout, _5_out, _6_2_cout, _6_out, _7_2_cout, _7_out, _8_2_cout, _8_out, _9_2_cout, _9_out,
       _10_2_cout, _10_out, _11_2_cout, _11_out, _12_2_cout, _12_out, _13_2_cout, _13_out, _14_2_cout,
       _14_out, _15_2_cout, _15_out, _16_2_cout, _16_out, _17_2_cout, _17_out, _18_2_cout, _18_out,
       _19_2_cout, _19_out, _20_2_cout, _20_out, _21_2_cout, _21_out, _22_2_cout, _22_out, _23_2_cout,
       _23_out, _24_2_cout, _24_out, _25_2_cout, _25_out, _26_2_cout, _26_out, _27_2_cout, _27_out,
       _28_2_cout, _28_out, _29_2_cout, _29_out, _30_2_cout, _30_out, _31_out;

  xor _0 (_0_out, B[0], ADD_SUB);
  xor _1 (_1_out, B[1], ADD_SUB);
  xor _2 (_2_out, B[2], ADD_SUB);
  xor _3 (_3_out, B[3], ADD_SUB);
  xor _4 (_4_out, B[4], ADD_SUB);
  xor _5 (_5_out, B[5], ADD_SUB);
  xor _6 (_6_out, B[6], ADD_SUB);
  xor _7 (_7_out, B[7], ADD_SUB);
  xor _8 (_8_out, B[8], ADD_SUB);
  xor _9 (_9_out, B[9], ADD_SUB);
  xor _10 (_10_out, B[10], ADD_SUB);
  xor _11 (_11_out, B[11], ADD_SUB);
  xor _12 (_12_out, B[12], ADD_SUB);
  xor _13 (_13_out, B[13], ADD_SUB);
  xor _14 (_14_out, B[14], ADD_SUB);
  xor _15 (_15_out, B[15], ADD_SUB);
  Full_Adder _0_2 (.Cin(ADD_SUB), .A(A[0]), .B(_0_out), .S(F[0]), .Cout(_0_2_cout));
  Full_Adder _1_2 (.Cin(_0_2_cout), .A(A[1]), .B(_1_out), .S(F[1]), .Cout(_1_2_cout));
  Full_Adder _2_2 (.Cin(_1_2_cout), .A(A[2]), .B(_2_out), .S(F[2]), .Cout(_2_2_cout));
  Full_Adder _3_2 (.Cin(_2_2_cout), .A(A[3]), .B(_3_out), .S(F[3]), .Cout(_3_2_cout));
  Full_Adder _4_2 (.Cin(_3_2_cout), .A(A[4]), .B(_4_out), .S(F[4]), .Cout(_4_2_cout));
  Full_Adder _5_2 (.Cin(_4_2_cout), .A(A[5]), .B(_5_out), .S(F[5]), .Cout(_5_2_cout));
  Full_Adder _6_2 (.Cin(_5_2_cout), .A(A[6]), .B(_6_out), .S(F[6]), .Cout(_6_2_cout));
  Full_Adder _7_2 (.Cin(_6_2_cout), .A(A[7]), .B(_7_out), .S(F[7]), .Cout(_7_2_cout));
  Full_Adder _8_2 (.Cin(_7_2_cout), .A(A[8]), .B(_8_out), .S(F[8]), .Cout(_8_2_cout));
  Full_Adder _9_2 (.Cin(_8_2_cout), .A(A[9]), .B(_9_out), .S(F[9]), .Cout(_9_2_cout));
  Full_Adder _10_2 (.Cin(_9_2_cout), .A(A[10]), .B(_10_out), .S(F[10]), .Cout(_10_2_cout));
  Full_Adder _11_2 (.Cin(_10_2_cout), .A(A[11]), .B(_11_out), .S(F[11]), .Cout(_11_2_cout));
  Full_Adder _12_2 (.Cin(_11_2_cout), .A(A[12]), .B(_12_out), .S(F[12]), .Cout(_12_2_cout));
  Full_Adder _13_2 (.Cin(_12_2_cout), .A(A[13]), .B(_13_out), .S(F[13]), .Cout(_13_2_cout));
  Full_Adder _14_2 (.Cin(_13_2_cout), .A(A[14]), .B(_14_out), .S(F[14]), .Cout(_14_2_cout));
  Full_Adder _15_2 (.Cin(_14_2_cout), .A(A[15]), .B(_15_out), .S(F[15]), .Cout(_15_2_cout));
  xor _16 (_16_out, B[16], ADD_SUB);
  xor _17 (_17_out, B[17], ADD_SUB);
  xor _18 (_18_out, B[18], ADD_SUB);
  xor _19 (_19_out, B[19], ADD_SUB);
  xor _20 (_20_out, B[20], ADD_SUB);
  xor _21 (_21_out, B[21], ADD_SUB);
  xor _22 (_22_out, B[22], ADD_SUB);
  xor _23 (_23_out, B[23], ADD_SUB);
  xor _24 (_24_out, B[24], ADD_SUB);
  xor _25 (_25_out, B[25], ADD_SUB);
  xor _26 (_26_out, B[26], ADD_SUB);
  xor _27 (_27_out, B[27], ADD_SUB);
  xor _28 (_28_out, B[28], ADD_SUB);
  xor _29 (_29_out, B[29], ADD_SUB);
  xor _30 (_30_out, B[30], ADD_SUB);
  xor _31 (_31_out, B[31], ADD_SUB);
  Full_Adder _16_2 (.Cin(_15_2_cout), .A(A[16]), .B(_16_out), .S(F[16]), .Cout(_16_2_cout));
  Full_Adder _17_2 (.Cin(_16_2_cout), .A(A[17]), .B(_17_out), .S(F[17]), .Cout(_17_2_cout));
  Full_Adder _18_2 (.Cin(_17_2_cout), .A(A[18]), .B(_18_out), .S(F[18]), .Cout(_18_2_cout));
  Full_Adder _19_2 (.Cin(_18_2_cout), .A(A[19]), .B(_19_out), .S(F[19]), .Cout(_19_2_cout));
  Full_Adder _20_2 (.Cin(_19_2_cout), .A(A[20]), .B(_20_out), .S(F[20]), .Cout(_20_2_cout));
  Full_Adder _21_2 (.Cin(_20_2_cout), .A(A[21]), .B(_21_out), .S(F[21]), .Cout(_21_2_cout));
  Full_Adder _22_2 (.Cin(_21_2_cout), .A(A[22]), .B(_22_out), .S(F[22]), .Cout(_22_2_cout));
  Full_Adder _23_2 (.Cin(_22_2_cout), .A(A[23]), .B(_23_out), .S(F[23]), .Cout(_23_2_cout));
  Full_Adder _24_2 (.Cin(_23_2_cout), .A(A[24]), .B(_24_out), .S(F[24]), .Cout(_24_2_cout));
  Full_Adder _25_2 (.Cin(_24_2_cout), .A(A[25]), .B(_25_out), .S(F[25]), .Cout(_25_2_cout));
  Full_Adder _26_2 (.Cin(_25_2_cout), .A(A[26]), .B(_26_out), .S(F[26]), .Cout(_26_2_cout));
  Full_Adder _27_2 (.Cin(_26_2_cout), .A(A[27]), .B(_27_out), .S(F[27]), .Cout(_27_2_cout));
  Full_Adder _28_2 (.Cin(_27_2_cout), .A(A[28]), .B(_28_out), .S(F[28]), .Cout(_28_2_cout));
  Full_Adder _29_2 (.Cin(_28_2_cout), .A(A[29]), .B(_29_out), .S(F[29]), .Cout(_29_2_cout));
  Full_Adder _30_2 (.Cin(_29_2_cout), .A(A[30]), .B(_30_out), .S(F[30]), .Cout(_30_2_cout));
  Full_Adder _31_2 (.Cin(_30_2_cout), .A(A[31]), .B(_31_out), .S(F[31]), .Cout(Cout));
  xor xor_1 (Overflow, Cout, _30_2_cout);
endmodule

module Full_Adder (
  input  Cin,
  input  A,
  input  B,
  output S,
  output Cout
);

  wire and_1_out, and_2_out, xor_1_out;

  xor xor_1 (xor_1_out, A, B);
  xor xor_2 (S, xor_1_out, Cin);
  and and_1 (and_1_out, Cin, xor_1_out);
  and and_2 (and_2_out, B, A);
  xor xor_3 (Cout, and_1_out, and_2_out);
endmodule

module comparator (
  input  [31:0] A,
  input  [31:0] B,
  input  [31:0] adder_result,
  input  overflow,
  input  cout,
  output [31:0] A_2
);

  wire or_1_out;
  wire [0:0] not_1_out, xor_1_out;

  xor xor_1 (xor_1_out[0], adder_result[31], overflow);
  not not_1 (not_1_out[0], cout);
  or or_1 (or_1_out, B[31], A[31]);
  Multiplexer #(.width(32)) multiplexer_1 (
    .in0({{31{1'b0}}, not_1_out[0]}), .in1({{31{1'b0}}, xor_1_out[0]}), .out(A_2), .sel(or_1_out));  // open: en
endmodule
