// Logisim project pipeline-registers.circ as structural Verilog: 3 circuits, main circuit EX
module EX (
  input  RegWrite,
  input  ExtOp,
  input  ALUSrc,
  input  [2:0] ALUOp,
  input  [5:0] func,
  input  MemRead,
  input  MemWrite,
  input  MemToReg,
  input  bne,
  input  beq,
  input  j,
  input  CLCK,
  input  Stall,
  output RegWrite_2,
  output ExtOp_2,
  output ALUSrc_2,
  output [2:0] ALUOp_2,
  output [5:0] func_2,
  output MemRead_2,
  output MemWrite_2,
  output MemToReg_2,
  output bne_2,
  output beq_2,
  output j_2
);

  wire multiplexer_1_out, multiplexer_2_out, multiplexer_3_out, multiplexer_6_out, multiplexer_7_out,
       multiplexer_8_out, multiplexer_9_out, multiplexer_10_out, multiplexer_11_out, not_1_out;
  wire [2:0] multiplexer_4_out;
  wire [5:0] multiplexer_5_out;

  Multiplexer #(.disabled(0), .enable("false")) multiplexer_1 (
    .in0(RegWrite), .in1(1'b0), .out(multiplexer_1_out), .sel(Stall));
  Multiplexer #(.disabled(0), .enable("false")) multiplexer_2 (
    .in0(ExtOp), .in1(1'b0), .out(multiplexer_2_out), .sel(Stall));
  Multiplexer #(.disabled(0), .enable("false")) multiplexer_3 (
    .in0(ALUSrc), .in1(1'b0), .out(multiplexer_3_out), .sel(Stall));
  Multiplexer #(.width(3), .disabled(0), .enable("false")) multiplexer_4 (
    .in0(ALUOp), .in1(3'b000), .out(multiplexer_4_out), .sel(Stall));
  Multiplexer #(.width(6), .disabled(0), .enable("false")) multiplexer_5 (
    .in0(func), .out(multiplexer_5_out), .sel(Stall));  // open: in1
  Multiplexer #(.disabled(0), .enable("false")) multiplexer_6 (
    .in0(MemRead), .in1(1'b0), .out(multiplexer_6_out), .sel(Stall));
  Multiplexer #(.disabled(0), .enable("false")) multiplexer_7 (
    .in0(MemWrite), .in1(1'b0), .out(multiplexer_7_out), .sel(Stall));
  Multiplexer #(.disabled(0), .enable("false")) multiplexer_8 (
    .in0(MemToReg), .in1(1'b0), .out(multiplexer_8_out), .sel(Stall));
  Multiplexer #(.disabled(0), .enable("false")) multiplexer_9 (
    .in0(bne), .in1(1'b0), .out(multiplexer_9_out), .sel(Stall));
  Multiplexer #(.disabled(0), .enable("false")) multiplexer_10 (
    .in0(beq), .in1(1'b0), .out(multiplexer_10_out), .sel(Stall));
  Multiplexer #(.disabled(0), .enable("false")) multiplexer_11 (
    .in0(j), .in1(1'b0), .out(multiplexer_11_out), .sel(Stall));
  Register #(.width(1)) register_1 (.D(multiplexer_1_out), .en(1'b1), .Q(RegWrite_2), .clk(CLCK), .clr(not_1_out));
  Register #(.width(1)) register_2 (.D(multiplexer_2_out), .en(1'b1), .Q(ExtOp_2), .clk(CLCK), .clr(not_1_out));
  Register #(.width(1)) register_3 (.D(multiplexer_3_out), .en(1'b1), .Q(ALUSrc_2), .clk(CLCK), .clr(not_1_out));
  Register #(.width(3)) register_4 (.D(multiplexer_4_out), .en(1'b1), .Q(ALUOp_2), .clk(CLCK), .clr(not_1_out));
  Register #(.width(6)) register_5 (.D(multiplexer_5_out), .en(1'b1), .Q(func_2), .clk(CLCK), .clr(not_1_out));
  Register #(.width(1)) register_6 (.D(multiplexer_6_out), .en(1'b1), .Q(MemRead_2), .clk(CLCK), .clr(not_1_out));
  Register #(.width(1)) register_7 (.D(multiplexer_7_out), .en(1'b1), .Q(MemWrite_2), .clk(CLCK), .clr(not_1_out));
  Register #(.width(1)) register_8 (.D(multiplexer_8_out), .en(1'b1), .Q(MemToReg_2), .clk(CLCK), .clr(not_1_out));
  Register #(.width(1)) register_9 (.D(multiplexer_9_out), .en(1'b1), .Q(bne_2), .clk(CLCK), .clr(not_1_out));
  Register #(.width(1)) register_10 (.D(multiplexer_10_out), .en(1'b1), .Q(beq_2), .clk(CLCK), .clr(not_1_out));
  Register #(.width(1)) register_11 (.D(multiplexer_11_out), .en(1'b1), .Q(j_2), .clk(CLCK), .clr(not_1_out));
  not not_1 (not_1_out, 1'b1);
endmodule

module MEM (
  input  MemRead,
  input  MemWrite,
  input  MemToReg,
  input  CLCK,
  input  RegWrite,
  output MemRead_2,
  output MemWrite_2,
  output MemToReg_2,
  output RegWrite_2
);

  wire not_1_out;

  not not_1 (not_1_out, 1'b1);
  Register #(.width(1)) register_1 (.D(MemRead), .en(1'b1), .Q(MemRead_2), .clk(CLCK), .clr(not_1_out));
  Register #(.width(1)) register_2 (.D(MemWrite), .en(1'b1), .Q(MemWrite_2), .clk(CLCK), .clr(not_1_out));
  Register #(.width(1)) register_3 (.D(MemToReg), .en(1'b1), .Q(MemToReg_2), .clk(CLCK), .clr(not_1_out));
  Register #(.width(1)) register_4 (.D(RegWrite), .en(1'b1), .Q(RegWrite_2), .clk(CLCK), .clr(not_1_out));
endmodule

module WB (
  input  RegWrite,
  input  CLK,
  output RegWrite_2
);

  wire not_1_out;

  not not_1 (not_1_out, 1'b1);
  Register #(.width(1)) register_1 (.D(RegWrite), .en(1'b1), .Q(RegWrite_2), .clk(CLK), .clr(not_1_out));
endmodule
