// Logisim project pipeline-stage-registers.circ as structural Verilog: 4 circuits, main circuit ID-stage
module EX_stage (
  input  [31:0] NPC2,
  input  [25:0] Imm26,
  input  [15:0] Imm16,
  input  [31:0] A,
  input  [31:0] B,
  input  [4:0] RD2,
  input  CLCK,
  output [31:0] NPC2_2,
  output [25:0] Imm26_2,
  output [15:0] Imm16_2,
  output [31:0] A_2,
  output [31:0] B_2,
  output [4:0] RD2_2
);

  wire not_1_out;

  Register #(.width(32)) register_1 (.D(NPC2), .en(1'b1), .Q(NPC2_2), .clk(CLCK), .clr(not_1_out));
  Register #(.width(26)) register_2 (.D(Imm26), .en(1'b1), .Q(Imm26_2), .clk(CLCK), .clr(not_1_out));
  Register #(.width(16)) register_3 (.D(Imm16), .en(1'b1), .Q(Imm16_2), .clk(CLCK), .clr(not_1_out));
  Register #(.width(32)) register_4 (.D(A), .en(1'b1), .Q(A_2), .clk(CLCK), .clr(not_1_out));
  Register #(.width(32)) register_5 (.D(B), .en(1'b1), .Q(B_2), .clk(CLCK), .clr(not_1_out));
  Register #(.width(5)) register_6 (.D(RD2), .en(1'b1), .Q(RD2_2), .clk(CLCK), .clr(not_1_out));
  not not_1 (not_1_out, 1'b1);
endmodule

module ID_stage (
  input  [31:0] NPC,
  input  CLCK,
  output [31:0] NPC_2
);

  wire not_1_out;

  Register #(.width(32)) register_1 (.D(NPC), .en(1'b1), .Q(NPC_2), .clk(CLCK), .clr(not_1_out));
  not not_1 (not_1_out, 1'b1);
endmodule

module MEM_stage (
  input  [31:0] ALUOut,
  input  [31:0] D,
  input  [4:0] RD3,
  input  CLCK,
  output [31:0] ALUOut_2,
  output [31:0] D_2,
  output [4:0] RD3_2
);

  wire not_1_out;

  Register #(.width(32)) register_1 (.D(ALUOut), .en(1'b1), .Q(ALUOut_2), .clk(CLCK), .clr(not_1_out));
  Register #(.width(32)) register_2 (.D(D), .en(1'b1), .Q(D_2), .clk(CLCK), .clr(not_1_out));
  Register #(.width(5)) register_3 (.D(RD3), .en(1'b1), .Q(RD3_2), .clk(CLCK), .clr(not_1_out));
  not not_1 (not_1_out, 1'b1);
endmodule

module WB_stage (
  input  [31:0] WBData,
  input  [4:0] RD4,
  input  CLCK,
  output [31:0] BusW,
  output [4:0] RD4_2
);

  wire not_1_out;

  Register #(.width(32)) register_1 (.D(WBData), .en(1'b1), .Q(BusW), .clk(CLCK), .clr(not_1_out));
  Register #(.width(5)) register_2 (.D(RD4), .en(1'b1), .Q(RD4_2), .clk(CLCK), .clr(not_1_out));
  not not_1 (not_1_out, 1'b1);
endmodule
